// Logisim project circ.circ as structural Verilog: 1 circuit, main circuit main
module main (
);

  wire and_1_out, and_2_out, and_3_out, and_4_out, and_5_out, and_6_out, and_7_out, and_8_out, and_9_out,
       button_1_out, clock_1_out, comparator_1_eq, comparator_2_eq, comparator_3_eq, comparator_4_eq,
       comparator_5_eq, comparator_6_eq, comparator_7_eq, comparator_8_eq, comparator_9_gt, not_1_out,
       not_2_out, not_3_out, or_1_out, or_2_out;
  wire [3:0] register_1_q, register_1_q_2, register_2_q, register_2_q_2, register_3_q, register_3_q_2;
  wire [7:0] adder_1_out, adder_2_out, adder_3_out, and_10_out, comparator_10_eq, controlled_buffer_1_out,
       counter_1_q, counter_2_q, divider_1_out, multiplexer_1_out, multiplexer_2_out, multiplexer_3_out,
       multiplier_1_out, multiplier_2_out, multiplier_3_out, nand_1_out, negator_1_out, nor_1_out, not_4_out,
       or_3_out, ram_1_dout, register_4_q, register_5_q, register_6_q, shifter_1_out, shifter_2_out,
       subtractor_1_out, xnor_1_out, xor_1_out;
  wire [15:8] ram_1_dout_2;
  wire [20:0] rom_1_data;

  Register register_1 (
    .D(controlled_buffer_1_out), .en(rom_1_data[20]), .Q({register_1_q_2, register_1_q}), .clk(and_1_out),
    .clr(button_1_out));
  assign controlled_buffer_1_out = rom_1_data[17] ? {register_1_q_2, register_1_q} : 8'bz;  // Controlled_Buffer controlled_buffer_1
  Register register_2 (
    .D(controlled_buffer_1_out), .en(rom_1_data[19]), .Q({register_2_q_2, register_2_q}), .clk(and_1_out),
    .clr(button_1_out));
  assign controlled_buffer_1_out = rom_1_data[16] ? {register_2_q_2, register_2_q} : 8'bz;  // Controlled_Buffer controlled_buffer_2
  Register register_3 (
    .D(controlled_buffer_1_out), .en(rom_1_data[18]), .Q({register_3_q_2, register_3_q}), .clk(and_1_out),
    .clr(button_1_out));
  assign controlled_buffer_1_out = rom_1_data[15] ? {register_3_q_2, register_3_q} : 8'bz;  // Controlled_Buffer controlled_buffer_3
  Register register_4 (
    .D(controlled_buffer_1_out), .en(rom_1_data[14]), .Q(register_4_q), .clk(and_1_out), .clr(button_1_out));
  Register register_5 (
    .D(controlled_buffer_1_out), .en(rom_1_data[13]), .Q(register_5_q), .clk(and_1_out), .clr(button_1_out));
  Register register_6 (
    .D(comparator_10_eq), .en(rom_1_data[12]), .Q(register_6_q), .clk(and_1_out), .clr(button_1_out));
  not not_1 (not_1_out, button_1_out);
  Clock clock_1 (.out(clock_1_out));
  and and_1 (and_1_out, clock_1_out, not_1_out);
  not not_2 (not_2_out, and_1_out);
  Comparator comparator_1 (.a(register_5_q), .b(8'h1d), .eq(comparator_1_eq));  // open: gt, lt
  Comparator comparator_2 (.a(register_5_q), .b(8'h1e), .eq(comparator_2_eq));  // open: gt, lt
  Comparator comparator_3 (.a(register_5_q), .b(8'h1f), .eq(comparator_3_eq));  // open: gt, lt
  Comparator comparator_4 (.a(register_5_q), .b(8'h20), .eq(comparator_4_eq));  // open: gt, lt
  Comparator comparator_5 (.a(register_5_q), .b(8'h21), .eq(comparator_5_eq));  // open: gt, lt
  Comparator comparator_6 (.a(register_5_q), .b(8'h22), .eq(comparator_6_eq));  // open: gt, lt
  Comparator comparator_7 (.a(register_5_q), .b(8'h23), .eq(comparator_7_eq));  // open: gt, lt
  Comparator comparator_8 (.a(register_5_q), .b(8'h24), .eq(comparator_8_eq));  // open: gt, lt
  Counter counter_1 (
    .load(rom_1_data[11]), .D(controlled_buffer_1_out), .count(rom_1_data[9]), .Q(counter_1_q),
    .clk(and_1_out), .clr(button_1_out));  // open: carry, up
  Counter #(.max('h7)) counter_2 (.Q(counter_2_q), .clk(not_3_out), .clr(or_1_out));  // open: load, D, count, carry, up
  not not_3 (not_3_out, and_1_out);
  or or_1 (or_1_out, button_1_out, rom_1_data[8]);
  RAM #(.dataWidth(16)) ram_1 (
    .addr(register_4_q), .we(rom_1_data[2]), .oe(1'b1), .clk(not_2_out),
    .din({{8{1'b0}}, controlled_buffer_1_out}), .dout({ram_1_dout_2, ram_1_dout}));
  assign controlled_buffer_1_out = rom_1_data[10] ? counter_1_q : 8'bz;  // Controlled_Buffer controlled_buffer_4
  Adder adder_1 (
    .a({register_1_q_2, register_1_q}), .b({register_2_q_2, register_2_q}), .out(adder_1_out),
    .cout(comparator_10_eq[7]));  // open: cin
  Subtractor subtractor_1 (
    .a({register_1_q_2, register_1_q}), .b({register_2_q_2, register_2_q}), .out(subtractor_1_out));  // open: bin, bout
  Multiplier multiplier_1 (
    .a({register_1_q_2, register_1_q}), .b({register_2_q_2, register_2_q}), .out(multiplier_1_out));  // open: cin, cout
  Divider divider_1 (
    .a({register_1_q_2, register_1_q}), .b({register_2_q_2, register_2_q}), .out(divider_1_out));  // open: upper, rem
  Negator negator_1 (.in({register_1_q_2, register_1_q}), .out(negator_1_out));
  Shifter shifter_1 (.in({register_1_q_2, register_1_q}), .\dist (register_2_q[2:0]), .out(shifter_1_out));
  Shifter #(.shift("lr")) shifter_2 (
    .in({register_1_q_2, register_1_q}), .\dist (register_2_q[2:0]), .out(shifter_2_out));
  and and_2 (and_2_out, comparator_1_eq, register_6_q[0]);
  and and_3 (and_3_out, comparator_2_eq, register_6_q[1]);
  and and_4 (and_4_out, comparator_3_eq, register_6_q[2]);
  and and_5 (and_5_out, comparator_4_eq, register_6_q[3]);
  and and_6 (and_6_out, comparator_5_eq, register_6_q[4]);
  and and_7 (and_7_out, comparator_6_eq, register_6_q[5]);
  and and_8 (and_8_out, comparator_7_eq, register_6_q[6]);
  and and_9 (and_9_out, comparator_8_eq, register_6_q[7]);
  Multiplexer #(.select(4), .width(8)) multiplexer_1 (
    .in0(adder_1_out), .in1(subtractor_1_out), .in2(multiplier_1_out), .in3(divider_1_out),
    .in4(negator_1_out), .in5(shifter_1_out), .in6(shifter_2_out), .in7(not_4_out), .in8(and_10_out),
    .in9(or_3_out), .in10(nand_1_out), .in11(nor_1_out), .in12(xor_1_out), .in13(xnor_1_out),
    .in14({register_1_q_2, register_1_q}), .out(multiplexer_1_out), .sel(rom_1_data[7:4]));  // open: in15
  assign controlled_buffer_1_out = rom_1_data[3] ? multiplexer_1_out : 8'bz;  // Controlled_Buffer controlled_buffer_5
  or or_2 (or_2_out, and_2_out, and_3_out, and_4_out, and_5_out, and_6_out, and_7_out, and_8_out, and_9_out);
  assign not_4_out = ~{register_1_q_2, register_1_q};  // NOT_Gate not_4, 8 bits wide
  assign and_10_out = {register_1_q_2, register_1_q} & {register_2_q_2, register_2_q};  // AND_Gate and_10, 8 bits wide
  assign or_3_out = {register_1_q_2, register_1_q} | {register_2_q_2, register_2_q};  // OR_Gate or_3, 8 bits wide
  assign nand_1_out = ~({register_1_q_2, register_1_q} & {register_2_q_2, register_2_q});  // NAND_Gate nand_1, 8 bits wide
  assign nor_1_out = ~({register_1_q_2, register_1_q} | {register_2_q_2, register_2_q});  // NOR_Gate nor_1, 8 bits wide
  assign xor_1_out = {register_1_q_2, register_1_q} ^ {register_2_q_2, register_2_q};  // XOR_Gate xor_1, 8 bits wide
  assign xnor_1_out = ~({register_1_q_2, register_1_q} ^ {register_2_q_2, register_2_q});  // XNOR_Gate xnor_1, 8 bits wide
  Button button_1 (.out(button_1_out));
  assign controlled_buffer_1_out = rom_1_data[1] ? ram_1_dout_2 : 8'bz;  // Controlled_Buffer controlled_buffer_6
  assign controlled_buffer_1_out = rom_1_data[0] ? ram_1_dout : 8'bz;  // Controlled_Buffer controlled_buffer_7
  Multiplier multiplier_2 (.a(register_5_q), .b(8'h8), .out(multiplier_2_out));  // open: cin, cout
  Hex_Digit_Display hex_digit_display_1 (.value(register_1_q_2));  // open: dp
  Hex_Digit_Display hex_digit_display_2 (.value(register_1_q));  // open: dp
  Adder adder_2 (.a(multiplier_2_out), .b(counter_2_q), .out(adder_2_out));  // open: cin, cout
  Comparator comparator_9 (.a(register_5_q), .b(8'h1c), .gt(comparator_9_gt));  // open: eq, lt
  Multiplexer #(.width(8)) multiplexer_2 (
    .in0(counter_2_q), .in1(adder_3_out), .out(multiplexer_2_out), .sel(or_2_out));
  Multiplier multiplier_3 (.a(8'h1c), .b(8'h8), .out(multiplier_3_out));  // open: cin, cout
  Adder adder_3 (.a(multiplier_3_out), .b(counter_2_q), .out(adder_3_out));  // open: cin, cout
  Comparator comparator_10 (
    .a({register_1_q_2, register_1_q}), .b({8{1'b0}}), .eq(comparator_10_eq[0]));  // open: gt, lt
  Comparator comparator_11 (
    .a({register_1_q_2, register_1_q}), .b({8{1'b0}}), .gt(comparator_10_eq[2]));  // open: eq, lt
  Comparator comparator_12 (
    .a({register_1_q_2, register_1_q}), .b({8{1'b0}}), .lt(comparator_10_eq[3]));  // open: gt, eq
  Comparator comparator_13 (
    .a({register_1_q_2, register_1_q}), .b({register_2_q_2, register_2_q}), .lt(comparator_10_eq[4]));  // open: gt, eq
  Comparator comparator_14 (
    .a({register_1_q_2, register_1_q}), .b({register_2_q_2, register_2_q}), .gt(comparator_10_eq[5]));  // open: eq, lt
  Comparator comparator_15 (
    .a({register_1_q_2, register_1_q}), .b({register_2_q_2, register_2_q}), .eq(comparator_10_eq[6]));  // open: gt, lt
  Hex_Digit_Display hex_digit_display_3 (.value(register_2_q_2));  // open: dp
  ROM #(.dataWidth(21)) rom_1 (.addr(multiplexer_3_out), .data(rom_1_data));
  Multiplexer #(.width(8)) multiplexer_3 (
    .in0(adder_2_out), .in1(multiplexer_2_out), .out(multiplexer_3_out), .sel(comparator_9_gt));
  not not_5 (comparator_10_eq[1], comparator_10_eq[0]);
  Hex_Digit_Display hex_digit_display_4 (.value(register_2_q));  // open: dp
  Hex_Digit_Display hex_digit_display_5 (.value(register_3_q_2));  // open: dp
  Hex_Digit_Display hex_digit_display_6 (.value(register_3_q));  // open: dp

  // Notes on the sheet:
  //   contents of rom_1 (hex, n*v repeats v):
  //   4400 2202 100 5*0 4400 2202 100001 100 4*0 4400 2202 80001 100 4*0 4400 2202 40001 100 4*0 4400 2202
  //   4001 100001 100 0 0 0 4400 2202 4001 80001 100 0 0 0 4400 2202 4001 40001 100 0 0 0 4400 2202 4001
  //   20004 100 0 0 0 4400 2202 4001 10004 100 0 0 0 4400 2202 4001 8004 100 0 0 0 4400 2202 4001 20004
  //   110000 80001 100 0 4400 2202 4001 20004 108000 40001 100 0 4400 2202 4001 10004 88000 40001 100 0
  //   4400 2202 101008 100 4*0 4400 2202 101018 100 4*0 4400 2202 101028 100 4*0 4400 2202 101038 100 4*0
  //   4400 2202 101048 100 4*0 4400 2202 101058 100 4*0 4400 2202 101068 100 4*0 4400 2202 101078 100 4*0
  //   4400 2202 101088 100 4*0 4400 2202 101098 100 4*0 4400 2202 1010a8 100 4*0 4400 2202 1010b8 100 4*0
  //   4400 2202 1010c8 100 4*0 4400 2202 1010d8 100 4*0 4400 2202 1010e8 100 4*0 4400 2202 801 100 4*0
  //   4400 2202 801 100
endmodule
